# Fritzing sketch Chat-RADIO-Fritzing-Schematic (saved by Fritzing 0.9.3b)

parts:
  NodeMCU-_ESP2866 = NodeMCU V1.0
  NRF24L01 = NRF24L01+ Breakout Board
  Bateria_de_Lítio = Battery Holders [package=lipo-1100mAh]  # not connected
  Carregador_de_bateria_de_Lítio = Power Cell LiPo Charger/Booster  # not connected

nets:
  N1: NodeMCU-_ESP2866.D0, NRF24L01.CE
  N2: NodeMCU-_ESP2866.D1, NRF24L01.CS
  3V3: NodeMCU-_ESP2866.3V3, NRF24L01.VCC
  N3: NodeMCU-_ESP2866.D5, NRF24L01.SCK
  N4: NodeMCU-_ESP2866.D6, NRF24L01.MISO
  N5: NodeMCU-_ESP2866.D7, NRF24L01.MOSI
  GND: NodeMCU-_ESP2866.GND, NRF24L01.GND

notes:
  V+
  GND
  CE
  CS
  MOSI
  MISO
  SCK
  D0
  D1
  D6
  D7
  D5
  3v

custom parts:
  NodeMCU V1.0: ESP8266 based NodeMCU
